# Fritzing sketch Final_Circuit (saved by Fritzing 0.9.3b)
breadboards: 1

parts:
  Part1 = Arduino Nano (Rev3.0)  # not connected
  J1 = Basic Servo
  J3 = Basic Servo
  SEN1 = Pulse Sensor [package=SIP-3]
  A1 = Sparkfun myroware muscle sensor V1  # not connected
  J2 = Basic Servo

nets:
  GND: J1.gnd, J3.gnd, J2.gnd
  VCC: J1.vcc, J3.vcc, SEN1.VCC, J2.vcc

notes:
  Crown servo
  Left servo
  Right servo

custom parts:
  Pulse Sensor: Pulse Sensor Optical Heart Beat Sensor
  Sparkfun myroware muscle sensor V1: The MyoWare Muscle Sensor is the latest revision of the Muscle Sensor of old, now with a new wearable design that allows you to attach biomedical sensor pads directly to the board itself getting rid of those pesky cables. This new board also includes a slew of other new features including, single-supply voltage of +3.1V to +5V, RAW EMG output, polarity protected power pins, indicator LEDs, and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
